// Logisim project processor_riscv.circ as structural Verilog
module ALU (
  input  [2:0] F,
  input  [31:0] B,
  input  [31:0] A,
  output zero,
  output [31:0] Y
);

  wire comparator_1_lt;
  wire [31:0] adder_1_out, and_1_out, bit_extender_1_out, multiplexer_1_out, not_1_out, or_1_out;

  assign not_1_out = ~B;  // NOT_Gate not_1, 32 bits wide
  Multiplexer #(.width(32), .enable("false")) multiplexer_1 (
    .in0(B), .in1(not_1_out), .out(multiplexer_1_out), .sel(F[0]));
  assign and_1_out = B & A;  // AND_Gate and_1, 32 bits wide
  assign or_1_out = B | A;  // OR_Gate or_1, 32 bits wide
  Adder #(.width(32)) adder_1 (.a(multiplexer_1_out), .b(A), .out(adder_1_out), .cin(F[0]));  // open: cout
  Comparator #(.width(32), .mode("unsigned")) comparator_1 (.a(B), .b(A), .lt(comparator_1_lt));  // open: gt, eq
  assign bit_extender_1_out = {{31{1'b0}}, comparator_1_lt};  // Bit_Extender bit_extender_1
  Multiplexer #(.select(3), .width(32), .enable("false")) multiplexer_2 (
    .in0(adder_1_out), .in1(adder_1_out), .in2(and_1_out), .in3(or_1_out), .in5(bit_extender_1_out), .out(Y),
    .sel(F));  // open: in4, in6, in7
  nor nor_1 (zero, Y[0], Y[1], Y[2], Y[3], Y[4], Y[5], Y[6], Y[7], Y[8], Y[9], Y[10], Y[11], Y[12], Y[13], Y[14], Y[15], Y[16], Y[17], Y[18], Y[19], Y[20], Y[21], Y[22], Y[23], Y[24], Y[25], Y[26], Y[27], Y[28], Y[29], Y[30], Y[31]);
endmodule

module Datapath (
  output [31:0] t2
);

  wire alu_1_zero, and_1_out, clock_1_out, controlunit_1_alusrc, controlunit_1_branch, controlunit_1_regwrite;
  wire [2:0] controlunit_1_alucontrol;
  wire [7:0] adder_1_out, bit_extender_3_out, multiplexer_1_out, register_1_q, shifter_1_out;
  wire [31:0] adder_2_out, alu_1_y, bit_extender_1_out, bit_extender_2_out, multiplexer_2_out,
       multiplexer_3_out, registerfile_1_rd1, registerfile_1_rd2, rom_1_data,
       \räta_ut_imm_för_branch_1_out_2 ;

  Clock clock_1 (.out(clock_1_out));
  Multiplexer #(.width(8), .enable("false")) multiplexer_1 (
    .in0(adder_1_out), .in1(bit_extender_3_out), .out(multiplexer_1_out), .sel(and_1_out));
  Register register_1 (.D(multiplexer_1_out), .Q(register_1_q), .clk(clock_1_out));  // open: en, clr
  Adder adder_1 (.a(register_1_q), .b(8'h4), .out(adder_1_out));  // open: cin, cout
  Shifter #(.shift("lr")) shifter_1 (.in(register_1_q), .\dist (3'b010), .out(shifter_1_out));
  ROM #(.dataWidth(32)) rom_1 (.addr(shifter_1_out), .data(rom_1_data));  // open: sel
  assign bit_extender_1_out = {{24{1'b0}}, register_1_q};  // Bit_Extender bit_extender_1
  assign bit_extender_2_out = {{20{rom_1_data[31]}}, rom_1_data[31:20]};  // Bit_Extender bit_extender_2
  \Räta_ut_IMM_för_branch  \räta_ut_imm_för_branch_1  (.in_1(rom_1_data), .out_2(\räta_ut_imm_för_branch_1_out_2 ));
  RegisterFile registerfile_1 (
    .CLK(clock_1_out), .A1(rom_1_data[17:15]), .WD3(alu_1_y), .A2(rom_1_data[22:20]),
    .WE3(controlunit_1_regwrite), .RD1(registerfile_1_rd1), .RD2(registerfile_1_rd2), .A3(rom_1_data[9:7]),
    .T2(t2));
  Multiplexer #(.width(32), .enable("false")) multiplexer_2 (
    .in0(bit_extender_2_out), .in1(\räta_ut_imm_för_branch_1_out_2 ), .out(multiplexer_2_out),
    .sel(controlunit_1_branch));
  Multiplexer #(.width(32), .enable("false")) multiplexer_3 (
    .in0(registerfile_1_rd2), .in1(multiplexer_2_out), .out(multiplexer_3_out), .sel(controlunit_1_alusrc));
  Adder #(.width(32)) adder_2 (.a(multiplexer_2_out), .b(bit_extender_1_out), .out(adder_2_out));  // open: cin, cout
  ControlUnit controlunit_1 (
    .Instruction(rom_1_data), .RegWrite(controlunit_1_regwrite), .ALUSrc(controlunit_1_alusrc),
    .ALUControl(controlunit_1_alucontrol), .Branch(controlunit_1_branch));
  Bit_Extender #(.in_width(32), .out_width(8)) bit_extender_3 (.in(adder_2_out), .out(bit_extender_3_out));
  and and_1 (and_1_out, controlunit_1_branch, alu_1_zero);
  ALU alu_1 (
    .F(controlunit_1_alucontrol), .B(multiplexer_3_out), .A(registerfile_1_rd1), .Y(alu_1_y),
    .zero(alu_1_zero));

  // Notes on the sheet:
  //   contents of rom_1 (hex, n*v repeats v):
  //   b00293 100393 2028463 313 213 520863 730333 120213 fe000ae3 6003b3 fff28293 fc000ee3 63 400293
  //   228393 5383b3 538663 ffd38393 fe000ce3 33
endmodule

module RegisterFile (
  input  CLK,
  input  [2:0] A1,
  input  [31:0] WD3,
  input  [2:0] A2,
  input  WE3,
  input  [2:0] A3,
  output [31:0] RD1,
  output [31:0] RD2,
  output [31:0] T2
);

  wire and_1_out, and_2_out, and_3_out, and_4_out, and_5_out, and_6_out, and_7_out, decoder_1_out0,
       decoder_1_out1, decoder_1_out2, decoder_1_out3, decoder_1_out4, decoder_1_out5, decoder_1_out6,
       decoder_1_out7, false_gate_1_out_3;
  wire [31:0] register_1_q, register_2_q, register_3_q, register_4_q, register_5_q, register_6_q,
       register_7_q;

  Decoder #(.select(3)) decoder_1 (
    .out0(decoder_1_out0), .out1(decoder_1_out1), .out2(decoder_1_out2), .out3(decoder_1_out3),
    .out4(decoder_1_out4), .out5(decoder_1_out5), .out6(decoder_1_out6), .out7(decoder_1_out7), .sel(A3));  // open: en
  False_gate false_gate_1 (.in_1(WE3), .in_2(decoder_1_out0), .out_3(false_gate_1_out_3));
  and and_1 (and_1_out, WE3, decoder_1_out1);
  and and_2 (and_2_out, WE3, decoder_1_out2);
  and and_3 (and_3_out, WE3, decoder_1_out3);
  and and_4 (and_4_out, WE3, decoder_1_out4);
  and and_5 (and_5_out, WE3, decoder_1_out5);
  and and_6 (and_6_out, WE3, decoder_1_out6);
  and and_7 (and_7_out, WE3, decoder_1_out7);
  Register #(.width(32)) register_1 (.D(WD3), .en(false_gate_1_out_3), .Q(register_1_q), .clk(CLK));  // open: clr
  Register #(.width(32)) register_2 (.D(WD3), .en(and_1_out), .Q(register_2_q), .clk(CLK));  // open: clr
  Register #(.width(32)) register_3 (.D(WD3), .en(and_2_out), .Q(register_3_q), .clk(CLK));  // open: clr
  Register #(.width(32)) register_4 (.D(WD3), .en(and_3_out), .Q(register_4_q), .clk(CLK));  // open: clr
  Register #(.width(32)) register_5 (.D(WD3), .en(and_4_out), .Q(register_5_q), .clk(CLK));  // open: clr
  Register #(.width(32)) register_6 (.D(WD3), .en(and_5_out), .Q(register_6_q), .clk(CLK));  // open: clr
  Register #(.width(32)) register_7 (.D(WD3), .en(and_6_out), .Q(register_7_q), .clk(CLK));  // open: clr
  Register #(.width(32)) register_8 (.D(WD3), .en(and_7_out), .Q(T2), .clk(CLK));  // open: clr
  Multiplexer #(.select(3), .width(32)) multiplexer_1 (
    .in0(register_1_q), .in1(register_2_q), .in2(register_3_q), .in3(register_4_q), .in4(register_5_q),
    .in5(register_6_q), .in6(register_7_q), .in7(T2), .out(RD1), .sel(A1));  // open: en
  Multiplexer #(.select(3), .width(32)) multiplexer_2 (
    .in0(register_1_q), .in1(register_2_q), .in2(register_3_q), .in3(register_4_q), .in4(register_5_q),
    .in5(register_6_q), .in6(register_7_q), .in7(T2), .out(RD2), .sel(A2));  // open: en
endmodule

module ControlUnit (
  input  [31:0] Instruction,
  output RegWrite,
  output ALUSrc,
  output [2:0] ALUControl,
  output Branch
);

  wire comparator_3_eq;

  Comparator #(.width(7), .mode("unsigned")) comparator_1 (
    .a(Instruction[6:0]), .b(7'b1100011), .eq(Branch));  // open: gt, lt
  Comparator #(.width(7), .mode("unsigned")) comparator_2 (
    .a(Instruction[6:0]), .b(7'b0010011), .eq(ALUSrc));  // open: gt, lt
  Comparator #(.width(7), .mode("unsigned")) comparator_3 (
    .a(Instruction[6:0]), .b(7'b0110011), .eq(comparator_3_eq));  // open: gt, lt
  or or_1 (RegWrite, ALUSrc, comparator_3_eq);
  assign ALUControl = {{2{1'b0}}, Branch};  // Bit_Extender bit_extender_1
endmodule

module Tests (
  output [31:0] Y,
  output [3:0] Y_2,
  output [7:0] Y_3
);


  assign Y = 32'hf4010207;
  assign Y_2 = 4'b0010;
  assign Y_3 = 8'h22;

  // Notes on the sheet:
  //   binary values in Logisim. Convince yourself how the bits are displayed.
  //   Example 1: A simple example that illustrates how 32-bit values are displayed as 
  //   Example 2) An example of how to extra certain bits from a (in this case) 32-bit wire. Here we extract the bits 8..11 from the 32-bit wire.
  //   Example 3) Sometimes it is useful to extra bits from different position and the re-assemble them. In this case, we extract bits 8..11 and bits 15..18 and assemble them into an 8-bit wire.
endmodule

module testa_saker (
  input  [31:0] in_1,
  input  [31:0] in_2,
  input  [4:0] in_3,
  output out_4,
  output [31:0] out_5
);

  wire bitselector_1_out;

  BitSelector #(.width(32)) bitselector_1 (.in(in_2), .out(bitselector_1_out), .sel(in_3));
  Comparator #(.width(32), .mode("unsigned")) comparator_1 (.a(in_1), .b(in_2), .lt(out_4));  // open: gt, eq
  assign out_5 = {{31{bitselector_1_out}}, bitselector_1_out};  // Bit_Extender bit_extender_1
endmodule

module False_gate (
  input  in_1,
  input  in_2,
  output out_3
);

  wire and_1_out, not_1_out;

  and and_1 (and_1_out, in_1, in_2);
  and and_2 (out_3, and_1_out, not_1_out);
  not not_1 (not_1_out, in_2);
endmodule

module \Räta_ut_IMM_för_branch  (
  input  [31:0] in_1,
  output [31:0] out_2
);

  wire [31:0] adder_1_out, adder_2_out, bit_extender_1_out, bit_extender_2_out, bit_extender_3_out,
       bit_extender_4_out, shifter_1_out, shifter_2_out, shifter_3_out, shifter_4_out;

  assign bit_extender_1_out = {{28{1'b0}}, in_1[11:8]};  // Bit_Extender bit_extender_1
  assign bit_extender_2_out = {{26{1'b0}}, in_1[30:25]};  // Bit_Extender bit_extender_2
  assign bit_extender_3_out = {{31{1'b0}}, in_1[7]};  // Bit_Extender bit_extender_3
  assign bit_extender_4_out = {{31{1'b0}}, in_1[31]};  // Bit_Extender bit_extender_4
  Shifter #(.width(32)) shifter_1 (.in(bit_extender_1_out), .\dist (5'b00001), .out(shifter_1_out));
  Shifter #(.width(32)) shifter_2 (.in(bit_extender_2_out), .\dist (5'b00101), .out(shifter_2_out));
  Shifter #(.width(32)) shifter_3 (.in(bit_extender_3_out), .\dist (5'b01011), .out(shifter_3_out));
  Shifter #(.width(32)) shifter_4 (.in(bit_extender_4_out), .\dist (5'b01100), .out(shifter_4_out));
  Adder #(.width(32)) adder_1 (.a(shifter_1_out), .b(shifter_2_out), .out(adder_1_out));  // open: cin, cout
  Adder #(.width(32)) adder_2 (.a(shifter_3_out), .b(shifter_4_out), .out(adder_2_out));  // open: cin, cout
  Adder #(.width(32)) adder_3 (.a(adder_1_out), .b(adder_2_out), .out(out_2));  // open: cin, cout
endmodule
